// Logisim project 25b6048_FullAdder_Logisim.circ as structural Verilog: 1 circuit, main circuit main
module main (
  input  X,
  input  Y,
  input  Carryin,
  output SUM,
  output CarryOut
);

  wire and_1_out, and_2_out, and_3_out, or_1_out, xor_1_out;

  xor xor_1 (xor_1_out, X, Y);
  and and_1 (and_1_out, X, Y);
  and and_2 (and_2_out, X, Carryin);
  and and_3 (and_3_out, Y, Carryin);
  xor xor_2 (SUM, xor_1_out, Carryin);
  or or_1 (or_1_out, and_1_out, and_2_out);
  or or_2 (CarryOut, or_1_out, and_3_out);
endmodule
