// Logisim project 25b6048_HalfAdder_Logisim.circ as structural Verilog: 1 circuit, main circuit main
module main (
  input  X,
  input  Y,
  output Sum,
  output Carry
);

  xor xor_1 (Sum, X, Y);
  and and_1 (Carry, X, Y);
endmodule
