// Logisim project 25b6048_LabExercise1_Logisim.circ as structural Verilog: 1 circuit, main circuit main
module main (
  input  X,
  input  Y,
  input  Z,
  output F
);

  wire notY_out, notYZ_out;

  not notY (notY_out, Y);
  and notYZ (notYZ_out, notY_out, Z);
  or XnotYZ (F, X, notYZ_out);
endmodule
