// Logisim project 25b6048_Multiplexer_Logisim.circ as structural Verilog: 1 circuit, main circuit main
module main (
  input  s1,
  input  s0,
  input  I3,
  input  I2,
  input  I1,
  input  I0,
  output Y
);

  wire A_out, B_out, C_out, D_out, not_1_out, not_2_out;

  not not_1 (not_1_out, s1);
  not not_2 (not_2_out, s0);
  and A (A_out, s1, s0, I3);
  and B (B_out, s1, not_2_out, I2);
  and C (C_out, not_1_out, s0, I1);
  and D (D_out, not_1_out, not_2_out, I0);
  or or_1 (Y, A_out, B_out, C_out, D_out);
endmodule
